# Fritzing sketch receiver (saved by Fritzing 0.9.1b)

parts:
  U1 = Arduino Uno (Rev3)
  U2 = RF-LINK_RX [package=rf-link_rx]
  LED1 = LED - 5mm [color="Red (633nm)" package="5 mm [THT]"]
  LCD1 = LCD screen
  R1 = Resistor [tolerance=±5% resistance=470 package=THT]
  R2 = Resistor [tolerance=±5% resistance=220 package=THT]
  R3 = Trimmer Potentiometer [maximum_resistance=10kΩ package=THT]

nets:
  GND: U1.GND, U2.GND, LED1.cathode
  N1: U1.D8, LCD1.E
  N2: U1.D9_PWM, LCD1.RS
  N3: U1.D10_PWM/SS, R1.Pin_0
  N4: U1.D12/MISO, U2.DATA
  N5: U1.D2, LCD1.DB7
  N6: U1.D3_PWM, LCD1.DB6
  N7: U1.D4, LCD1.DB5
  N8: U1.D5_PWM, LCD1.DB4
  5V: U1.5V, U2.+5V
  N9: LED1.anode, R1.Pin_1
  N10: LCD1.V0, R3.wiper
  N11: LCD1.LED+, R2.Pin_0
