# Fritzing sketch transmitter (saved by Fritzing 0.9.1b)

parts:
  U2 = RF-LINK_TX [package=rf-link_tx]
  U4 = SRF05 Ultrasonic Rangefinder
  U3 = SRF05 Ultrasonic Rangefinder
  U1 = Arduino Uno (Rev3)

nets:
  N1: U2.DATA, U1.D10_PWM/SS
  VCC: U4.VCC, U3.VCC
  N2: U4.Trig, U1.D12/MISO
  N3: U4.Echo, U1.D11_PWM/MOSI
  GND: U4.GND, U3.GND
